# Fritzing sketch Pi Pico telegraph sounder (saved by Fritzing 0.9.6b)
circuit board: 6.27076cm x 6.43238cm
breadboards: 1

parts:
  D1 = Rectifier Diode [part_number=1N4001 package="300 mil [THT]"]
  R1 = Resistor [resistance=1k tolerance=±5% power=0.25 package=THT]
  Q1 = NPN-Transistor [package="TO92 [THT]"]
  VCC1 = 4 x AAA Battery Mount
  S2 = Momentary Switch [package=ksa_sealed_tac_switch]
  Mod1 = rpi_pico-tht_1
  S3 = Momentary Switch [package=ksa_sealed_tac_switch]
  L1 = Inductor [package="0603 [SMD]"]

nets (from the breadboard view):
  N1: D1.cathode, Q1.C, L1.pin_1
  N2: D1.anode, Q1.E
  N3: R1.Pin_0, Mod1.connector19
  N4: R1.Pin_1, Q1.B
  N5: VCC1.-, Mod1.connector37
  N6: VCC1.+, Mod1.connector38, L1.pin_0
  N7: S2.1, S2.2, Mod1.connector35, S3.3, S3.4
  N8: S2.3, S2.4, Mod1.connector18
  N9: Mod1.connector16, S3.1, S3.2

notes:
  Telegraph repeater coil
